// Logisim project ex1.circ as structural Verilog: 1 circuit, main circuit generate_immediate
module generate_immediate (
  input  [31:0] INSTRUCTION,
  output [31:0] IMMEDIATE
);

  Multiplexer #(.width(21)) multiplexer_1 (
    .in0({21{1'b0}}), .in1({21{1'b1}}), .out(IMMEDIATE[31:11]), .sel(INSTRUCTION[31]));

  assign IMMEDIATE[10:0] = {INSTRUCTION[30:25], INSTRUCTION[11:7]};

  // Other names for the same wires on the sheet: imm_0_4[4:0] = INSTRUCTION[11:7]; imm_5_11[6:0] = INSTRUCTION[31:25];
  //   opcode[6:0] = INSTRUCTION[6:0]; funct3[2:0] = INSTRUCTION[14:12]; rs1[4:0] = INSTRUCTION[19:15];
  //   rs2[4:0] = INSTRUCTION[24:20]
endmodule
